# Fritzing sketch specs (saved by Fritzing 0.9.3b)

parts:
  LED1 = smd LED [color="Orange (620nm)" package="1206 [SMD]"]  # not connected
  LED2 = smd LED [color="Orange (620nm)" package="1206 [SMD]"]  # not connected
  LED3 = smd LED [color="Orange (620nm)" package="1206 [SMD]"]
  LED4 = smd LED [color="Orange (620nm)" package="1206 [SMD]"]  # not connected
  LED5 = smd LED [color="Orange (620nm)" package="1206 [SMD]"]  # not connected
  LED6 = smd LED [color="Orange (620nm)" package="1206 [SMD]"]  # not connected
  LED7 = smd LED [color="Orange (620nm)" package="1206 [SMD]"]  # not connected
  LED8 = smd LED [color="Orange (620nm)" package="1206 [SMD]"]
  LED9 = smd LED [color="Orange (620nm)" package="1206 [SMD]"]  # not connected
  LED10 = smd LED [color="Orange (620nm)" package="1206 [SMD]"]  # not connected
  LED11 = smd LED [color="Orange (620nm)" package="1206 [SMD]"]  # not connected
  LED12 = smd LED [color="Orange (620nm)" package="1206 [SMD]"]  # not connected
  LED13 = smd LED [color="Orange (620nm)" package="1206 [SMD]"]  # not connected
  LED14 = smd LED [color="Orange (620nm)" package="1206 [SMD]"]  # not connected
  LED15 = smd LED [color="Orange (620nm)" package="1206 [SMD]"]  # not connected
  LED16 = smd LED [color="Orange (620nm)" package="1206 [SMD]"]  # not connected
  LED17 = smd LED [color="Orange (620nm)" package="1206 [SMD]"]  # not connected
  LED18 = smd LED [color="Orange (620nm)" package="1206 [SMD]"]  # not connected
  LED19 = smd LED [color="Orange (620nm)" package="1206 [SMD]"]  # not connected
  LED20 = smd LED [color="Orange (620nm)" package="1206 [SMD]"]  # not connected
  LED21 = smd LED [color="Orange (620nm)" package="1206 [SMD]"]  # not connected
  LED22 = smd LED [color="Orange (620nm)" package="1206 [SMD]"]  # not connected
  LED23 = smd LED [color="Orange (620nm)" package="1206 [SMD]"]  # not connected
  LED24 = smd LED [color="Orange (620nm)" package="1206 [SMD]"]  # not connected
  LED25 = smd LED [color="Orange (620nm)" package="1206 [SMD]"]
  LED26 = smd LED [color="Orange (620nm)" package="1206 [SMD]"]
  LED27 = smd LED [color="Orange (620nm)" package="1206 [SMD]"]
  LED28 = smd LED [color="Orange (620nm)" package="1206 [SMD]"]
  LED29 = smd LED [color="Orange (620nm)" package="1206 [SMD]"]
  LED30 = smd LED [color="Orange (620nm)" package="1206 [SMD]"]
  LED31 = smd LED [color="Orange (620nm)" package="1206 [SMD]"]
  LED32 = smd LED [color="Orange (620nm)" package="1206 [SMD]"]
  IC1 = IC, DIP package, 16 pins [chip_label=IC]

nets:
  N1: LED3.anode, LED8.anode
  N2: LED25.cathode, IC1.pin11
  N3: LED26.cathode, IC1.pin12
  N4: LED27.cathode, IC1.pin7
  N5: LED28.cathode, IC1.pin9
  N6: LED29.cathode, IC1.pin6
  N7: LED30.cathode, IC1.pin4
  N8: LED31.cathode, IC1.pin10
  N9: LED32.cathode, IC1.pin5
